# Fritzing sketch dioda-sveti-tipka (saved by Fritzing 0.9.2b)
breadboards: 1

parts:
  Part1 = Arduino Uno (Rev3)
  LED1 = LED - 5mm [color="Red (633nm)" package="5 mm [THT]"]
  R1 = Resistor [tolerance=±5% resistance=1k package=THT]
  S1 = Pushbutton [package="[THT]"]

nets:
  N1: Part1.5V, R1.Pin_0
  N2: Part1.GND, LED1.cathode
  N3: LED1.anode, S1.Pin_1, S1.Pin_2
  N4: R1.Pin_1, S1.Pin_3, S1.Pin_4
