# Fritzing sketch lcd-tipka (saved by Fritzing 0.9.2b)
circuit board: 8.46667cm x 5.64444cm
breadboards: 1

parts:
  Part1 = Arduino Uno (Rev3)
  LCD1 = LCD screen
  R1 = Trimmer Potentiometer [maximum_resistance=10kΩ package=THT]
  S1 = Pushbutton [package="[THT]"]
  R2 = Resistor [tolerance=±5% resistance=1k package=THT]

nets:
  N1: Part1.D10_PWM/SS, LCD1.E
  N2: Part1.D11_PWM/MOSI, LCD1.R/W
  N3: Part1.D12/MISO, LCD1.RS
  GND: Part1.GND, LCD1.VSS, LCD1.LED-
  N4: Part1.D2, LCD1.DB7
  N5: Part1.D3_PWM, LCD1.DB6
  N6: Part1.D4, LCD1.DB5
  N7: Part1.D5_PWM, LCD1.DB4
  N8: Part1.D7, S1.Pin_3, S1.Pin_4, R2.Pin_1
  5V: Part1.5V, LCD1.VDD, LCD1.LED+
  N9: LCD1.V0, R1.wiper
  N10: R1.leg1, R2.Pin_0
  N11: R1.leg2, S1.Pin_1, S1.Pin_2
