# Fritzing sketch ledica-tipka-interrupt (saved by Fritzing 0.9.2b)
breadboards: 1

parts:
  Part1 = Arduino Uno (Rev3)
  LED1 = LED - 5mm [color="Red (633nm)" package="5 mm [THT]"]
  R1 = Resistor [tolerance=±5% resistance=1k package=THT]
  S1 = Pushbutton [package="[THT]"]
  R2 = Resistor [tolerance=±5% resistance=10k package=THT]

nets:
  N1: Part1.D2, S1.Pin_3, S1.Pin_4, R2.Pin_1
  N2: Part1.5V, S1.Pin_1, S1.Pin_2
  N3: Part1.GND, R1.Pin_0, R2.Pin_0
  N4: LED1.cathode, R1.Pin_1
