# Fritzing sketch 1.5-semafor (saved by Fritzing 0.9.2b)
breadboards: 1

parts:
  Part1 = Arduino Uno (Rev3)
  LED1 = LED - 5mm [color="Red (633nm)" package="5 mm [THT]"]
  R1 = Resistor [tolerance=±5% resistance=220 package=THT]
  R2 = Resistor [tolerance=±5% resistance=220 package=THT]
  R3 = Resistor [tolerance=±5% resistance=220 package=THT]
  LED2 = LED - 5mm [color="Orange (612nm)" package="5 mm [THT]"]
  LED3 = LED - 5mm [color="Green (565nm)" package="5 mm [THT]"]

nets:
  N1: Part1.GND, R1.Pin_0, R2.Pin_0, R3.Pin_0
  N2: Part1.D3_PWM, LED1.anode
  N3: Part1.D4, LED2.anode
  N4: Part1.D5_PWM, LED3.anode
  N5: LED1.cathode, R3.Pin_1
  N6: R1.Pin_1, LED3.cathode
  N7: R2.Pin_1, LED2.cathode
