# Fritzing sketch 5.1-dve-tipki (saved by Fritzing 0.9.2b)
breadboards: 1

parts:
  Part1 = Arduino Uno (Rev3)
  R1 = Resistor [tolerance=±5% resistance=220 package=THT]
  LED1 = LED - 5mm [color="Red (633nm)" package="5 mm [THT]"]
  S1 = Pushbutton [package="[THT]"]
  S2 = Pushbutton [package="[THT]"]
  R2 = Resistor [tolerance=±5% resistance=220 package=THT]
  LED2 = LED - 5mm [color="Red (633nm)" package="5 mm [THT]"]

nets:
  N1: Part1.D10_PWM/SS, S1.Pin_1, S1.Pin_2
  N2: Part1.D11_PWM/MOSI, S2.Pin_1, S2.Pin_2
  N3: Part1.GND, R1.Pin_0, S1.Pin_3, S1.Pin_4, S2.Pin_3, S2.Pin_4, R2.Pin_0
  N4: Part1.D3_PWM, LED2.anode
  N5: Part1.D4, LED1.anode
  N6: R1.Pin_1, LED1.cathode
  N7: R2.Pin_1, LED2.cathode
